// Logisim project proj_2_2.circ as structural Verilog: 3 circuits, main circuit testbench
module inst_fetch (
  input  clk,
  input  rst,
  input  control_en_i,
  input  [31:0] control_pc_i,
  input  [15:0] inst_i,
  output inst_en_o,
  output [31:0] current_pc_o,
  output [31:0] inst_addr_o,
  output [15:0] inst_o
);

  wire not_1_out, not_2_out;
  wire [31:0] adder_1_out, counter_1_q, multiplexer_1_out;

  not not_1 (not_1_out, rst);
  Adder #(.width(32)) adder_1 (.a(control_pc_i), .b(32'h1), .out(adder_1_out));  // open: cin, cout
  Counter #(.max('hffffffff), .width(32)) counter_1 (
    .clr(rst), .load(control_en_i), .up(not_1_out), .count(not_1_out), .clk(clk), .D(adder_1_out),
    .Q(counter_1_q));  // open: carry
  Multiplexer #(.width(32)) multiplexer_1 (
    .in0(counter_1_q), .in1(control_pc_i), .out(multiplexer_1_out), .sel(control_en_i));
  not not_2 (not_2_out, rst);
  Register #(.width(32)) register_1 (.D(multiplexer_1_out), .en(not_2_out), .clk(clk), .Q(current_pc_o), .clr(rst));
  not not_3 (inst_en_o, rst);

  assign inst_addr_o = current_pc_o;
  assign inst_o = inst_i;

  // Notes on the sheet:
  //   Don't touch
endmodule

module TOP (
  input  in_1,
  input  in_2,
  input  [15:0] in_3,
  input  [31:0] in_4,
  input  [31:0] in_5,
  output out_6,
  output [31:0] out_7,
  output out_8,
  output [31:0] out_9,
  output out_10,
  output [31:0] out_11,
  output out_12,
  output [4:0] out_13,
  output [31:0] out_14
);

  wire and_12_out, and_14_out, and_15_out, and_18_out, and_19_out, and_20_out, and_21_out, and_22_out,
       and_23_out, and_24_out, and_25_out, and_26_out, and_27_out, and_28_out, and_29_out, and_30_out,
       and_31_out, and_32_out, comparator_1_eq, comparator_2_eq, comparator_3_eq, comparator_4_eq,
       comparator_5_eq, comparator_6_eq, comparator_7_eq, comparator_8_eq, comparator_9_eq, comparator_10_eq,
       comparator_11_eq, comparator_12_eq, comparator_13_eq, comparator_14_eq, comparator_15_eq,
       comparator_16_eq, comparator_17_eq, comparator_18_eq, comparator_19_eq, comparator_20_eq,
       comparator_21_eq, comparator_22_eq, comparator_23_eq, comparator_24_eq, comparator_25_eq,
       comparator_26_eq, comparator_27_eq, comparator_28_eq, comparator_29_eq, comparator_30_eq,
       comparator_31_eq, demultiplexer_1_out0, demultiplexer_1_out2, demultiplexer_1_out8,
       demultiplexer_1_out9, demultiplexer_1_out10, demultiplexer_1_out11, demultiplexer_1_out12,
       demultiplexer_1_out13, demultiplexer_1_out14, demultiplexer_1_out15, demultiplexer_2_out0,
       demultiplexer_2_out1, demultiplexer_2_out2, demultiplexer_2_out3, demultiplexer_2_out4,
       demultiplexer_2_out5, demultiplexer_2_out6, demultiplexer_2_out7, \do , is_add, is_addi, is_addi4spn,
       is_beqz, is_j, is_jr, is_li, is_lui, is_lw, is_mv, is_new, is_nop, is_old, is_slli, is_sw, is_swsp,
       is_x2, not_1_out, or_2_out, or_3_out, or_4_out, or_5_out, or_6_out, or_7_out, or_8_out, or_11_out,
       or_12_out, or_13_out, wpc;
  wire [4:0] bit_extender_4_out, multiplexer_19_out, multiplexer_26_out, new_reg_sel, reg_wsel;
  wire [31:0] adder_10_out, addi4spn_imm, addr_lw, addr_sw, addr_swsp, alu_add, alu_addi, alu_addi4spn,
       alu_beqz, alu_j, alu_jr, alu_li, alu_lui, alu_mv, alu_new, alu_result_new, alu_result_old, alu_slli,
       alu_sw, dpc, multiplexer_1_out, multiplexer_3_out, multiplexer_5_out, multiplexer_7_out,
       multiplexer_17_out, multiplexer_18_out, multiplexer_20_out, multiplexer_21_out, multiplexer_23_out,
       multiplexer_24_out, multiplexer_25_out, multiplexer_27_out, multiplexer_29_out, multiplexer_31_out,
       multiplexer_32_out, multiplexer_33_out, multiplexer_35_out, multiplexer_36_out, multiplexer_37_out,
       multiplexer_39_out, offset_beqz, offset_j, out_0, out_2, out_8_t, out_9_t, out_10_t, out_11_t,
       out_12_t, out_13_t, out_14_t, out_15, rs1_new, swsp_imm, uimm_lsw;

  Comparator #(.width(2)) comparator_1 (.a(2'b10), .b(in_3[1:0]), .eq(comparator_1_eq));  // open: gt, lt
  Comparator #(.width(4)) comparator_2 (.a(4'b1001), .b(in_3[15:12]), .eq(comparator_2_eq));  // open: gt, lt
  Comparator #(.width(2)) comparator_3 (.a(2'b10), .b(in_3[1:0]), .eq(comparator_3_eq));  // open: gt, lt
  Comparator #(.width(4)) comparator_4 (.a(4'b1000), .b(in_3[15:12]), .eq(comparator_4_eq));  // open: gt, lt
  Comparator #(.width(2)) comparator_5 (.a(2'b01), .b(in_3[1:0]), .eq(comparator_5_eq));  // open: gt, lt
  Comparator #(.width(3)) comparator_6 (.a(3'b000), .b(in_3[15:13]), .eq(comparator_6_eq));  // open: gt, lt
  Comparator #(.width(2)) comparator_7 (.a(2'b10), .b(in_3[1:0]), .eq(comparator_7_eq));  // open: gt, lt
  Comparator #(.width(3)) comparator_8 (.a(3'b000), .b(in_3[15:13]), .eq(comparator_8_eq));  // open: gt, lt
  Comparator #(.width(2)) comparator_9 (.a(2'b01), .b(in_3[1:0]), .eq(comparator_9_eq));  // open: gt, lt
  Comparator #(.width(3)) comparator_10 (.a(3'b010), .b(in_3[15:13]), .eq(comparator_10_eq));  // open: gt, lt
  Comparator #(.width(2)) comparator_11 (.a(2'b01), .b(in_3[1:0]), .eq(comparator_11_eq));  // open: gt, lt
  Comparator #(.width(3)) comparator_12 (.a(3'b011), .b(in_3[15:13]), .eq(comparator_12_eq));  // open: gt, lt
  Comparator #(.width(2)) comparator_13 (.a(2'b01), .b(in_3[1:0]), .eq(comparator_13_eq));  // open: gt, lt
  Comparator #(.width(3)) comparator_14 (.a(3'b000), .b(in_3[15:13]), .eq(comparator_14_eq));  // open: gt, lt
  Comparator #(.width(2)) comparator_15 (.a(2'b10), .b(in_3[1:0]), .eq(comparator_15_eq));  // open: gt, lt
  Comparator #(.width(3)) comparator_16 (.a(3'b110), .b(in_3[15:13]), .eq(comparator_16_eq));  // open: gt, lt
  Comparator #(.width(2)) comparator_17 (.a(2'b00), .b(in_3[1:0]), .eq(comparator_17_eq));  // open: gt, lt
  Comparator #(.width(3)) comparator_18 (.a(3'b000), .b(in_3[15:13]), .eq(comparator_18_eq));  // open: gt, lt
  Comparator #(.width(2)) comparator_19 (.a(2'b00), .b(in_3[1:0]), .eq(comparator_19_eq));  // open: gt, lt
  Comparator #(.width(3)) comparator_20 (.a(3'b010), .b(in_3[15:13]), .eq(comparator_20_eq));  // open: gt, lt
  Comparator #(.width(2)) comparator_21 (.a(2'b00), .b(in_3[1:0]), .eq(comparator_21_eq));  // open: gt, lt
  Comparator #(.width(3)) comparator_22 (.a(3'b110), .b(in_3[15:13]), .eq(comparator_22_eq));  // open: gt, lt
  Comparator #(.width(2)) comparator_23 (.a(2'b01), .b(in_3[1:0]), .eq(comparator_23_eq));  // open: gt, lt
  Comparator #(.width(3)) comparator_24 (.a(3'b110), .b(in_3[15:13]), .eq(comparator_24_eq));  // open: gt, lt
  Adder #(.width(32)) adder_1 (.a(alu_jr), .b(alu_mv), .out(alu_add));  // open: cin, cout
  Adder #(.width(32)) adder_2 (.a(alu_jr), .b(alu_li), .out(alu_addi));  // open: cin, cout
  Shifter #(.width(32)) shifter_1 (.in(alu_jr), .\dist (in_3[6:2]), .out(alu_slli));
  Multiplexer #(.width(32)) multiplexer_1 (.in0({32{1'b0}}), .in1(addr_sw), .out(multiplexer_1_out), .sel(is_sw));
  or or_1 (is_x2, is_swsp, is_addi4spn);
  Multiplexer #(.width(5)) multiplexer_2 (.in0(in_3[11:7]), .in1(5'b00010), .out(reg_wsel), .sel(is_x2));
  Demultiplexer #(.select(5)) demultiplexer_1 (
    .out0(demultiplexer_1_out0), .out2(demultiplexer_1_out2), .out8(demultiplexer_1_out8),
    .out9(demultiplexer_1_out9), .out10(demultiplexer_1_out10), .out11(demultiplexer_1_out11),
    .out12(demultiplexer_1_out12), .out13(demultiplexer_1_out13), .out14(demultiplexer_1_out14),
    .out15(demultiplexer_1_out15), .in(1'b1), .sel(reg_wsel));  // open: out1, out3, out4, out5, out6, out7, out16, out17, out18, out19, out20, out21, out22, out23, out24, out25, out26, out27, out28, out29, out30, out31
  and and_1 (is_add, comparator_1_eq, comparator_2_eq);
  and and_2 (is_addi, comparator_5_eq, comparator_6_eq);
  and and_3 (is_slli, comparator_7_eq, comparator_8_eq);
  and and_4 (is_li, comparator_9_eq, comparator_10_eq);
  and and_5 (is_lui, comparator_11_eq, comparator_12_eq);
  and and_6 (is_nop, comparator_13_eq, comparator_14_eq);
  and and_7 (is_swsp, comparator_15_eq, comparator_16_eq);
  and and_8 (is_addi4spn, comparator_17_eq, comparator_18_eq);
  and and_9 (is_lw, comparator_19_eq, comparator_20_eq);
  and and_10 (is_sw, comparator_21_eq, comparator_22_eq);
  and and_11 (is_beqz, comparator_23_eq, comparator_24_eq);
  Comparator #(.width(5)) comparator_25 (.a(in_3[6:2]), .b({5{1'b0}}), .eq(comparator_25_eq));  // open: gt, lt
  Shifter #(.width(32)) shifter_2 (.in(alu_li), .\dist (5'b01100), .out(alu_lui));
  Multiplexer #(.width(32)) multiplexer_3 (
    .in0(multiplexer_1_out), .in1(addr_swsp), .out(multiplexer_3_out), .sel(is_swsp));
  Register #(.width(32)) register_1 (.D(out_9), .en(1'b0), .clk(in_2), .Q(out_0), .clr(in_1));
  Multiplexer #(.select(5), .width(32)) multiplexer_4 (
    .in0(out_0), .in2(out_2), .in8(out_8_t), .in9(out_9_t), .in10(out_10_t), .in11(out_11_t),
    .in12(out_12_t), .in13(out_13_t), .in14(out_14_t), .in15(out_15), .out(alu_jr), .sel(reg_wsel));  // open: in1, in3, in4, in5, in6, in7, in16, in17, in18, in19, in20, in21, in22, in23, in24, in25, in26, in27, in28, in29, in30, in31
  not not_1 (not_1_out, comparator_25_eq);
  assign alu_li = {{26{in_3[12]}}, {in_3[12], in_3[6:2]}};  // Bit_Extender bit_extender_1
  and and_12 (and_12_out, is_old, demultiplexer_1_out2);
  Register #(.width(32)) register_2 (.D(out_9), .en(and_12_out), .clk(in_2), .Q(out_2), .clr(in_1));
  and and_13 (is_mv, comparator_3_eq, not_1_out, comparator_4_eq);
  Multiplexer #(.width(32)) multiplexer_5 (
    .in0(multiplexer_3_out), .in1(addr_lw), .out(multiplexer_5_out), .sel(is_lw));
  and and_14 (and_14_out, is_old, demultiplexer_1_out8);
  or or_2 (or_2_out, and_14_out, and_24_out);
  Register #(.width(32)) register_3 (.D(out_9), .en(or_2_out), .clk(in_2), .Q(out_8_t), .clr(in_1));
  Multiplexer #(.select(5), .width(32)) multiplexer_6 (
    .in0(out_0), .in2(out_2), .in8(out_8_t), .in9(out_9_t), .in10(out_10_t), .in11(out_11_t),
    .in12(out_12_t), .in13(out_13_t), .in14(out_14_t), .in15(out_15), .out(alu_mv), .sel(in_3[6:2]));  // open: in1, in3, in4, in5, in6, in7, in16, in17, in18, in19, in20, in21, in22, in23, in24, in25, in26, in27, in28, in29, in30, in31
  Comparator #(.width(2)) comparator_26 (.a(2'b01), .b(in_3[1:0]), .eq(comparator_26_eq));  // open: gt, lt
  Comparator #(.width(3)) comparator_27 (.a(3'b101), .b(in_3[15:13]), .eq(comparator_27_eq));  // open: gt, lt
  Comparator #(.width(2)) comparator_28 (.a(2'b10), .b(in_3[1:0]), .eq(comparator_28_eq));  // open: gt, lt
  Comparator #(.width(3)) comparator_29 (.a(3'b100), .b(in_3[15:13]), .eq(comparator_29_eq));  // open: gt, lt
  Comparator #(.width(5)) comparator_30 (.a(in_3[6:2]), .b({5{1'b0}}), .eq(comparator_30_eq));  // open: gt, lt
  Multiplexer #(.width(32)) multiplexer_7 (
    .in0(multiplexer_5_out), .in1(alu_addi4spn), .out(multiplexer_7_out), .sel(is_addi4spn));
  and and_15 (and_15_out, is_old, demultiplexer_1_out9);
  or or_3 (or_3_out, and_15_out, and_25_out);
  Register #(.width(32)) register_4 (.D(out_9), .en(or_3_out), .clk(in_2), .Q(out_9_t), .clr(in_1));
  and and_16 (is_j, comparator_26_eq, comparator_27_eq);
  and and_17 (is_jr, comparator_28_eq, comparator_30_eq, comparator_29_eq);
  Adder #(.width(32)) adder_3 (.a(alu_jr), .b(swsp_imm), .out(addr_swsp));  // open: cin, cout
  Adder #(.width(32)) adder_4 (.a(addi4spn_imm), .b(alu_jr), .out(alu_addi4spn));  // open: cin, cout
  Adder #(.width(32)) adder_5 (.a(uimm_lsw), .b(rs1_new), .out(addr_lw));  // open: cin, cout
  Adder #(.width(32)) adder_6 (.a(uimm_lsw), .b(rs1_new), .out(addr_sw));  // open: cin, cout
  and and_18 (and_18_out, is_old, demultiplexer_1_out10);
  or or_4 (or_4_out, and_18_out, and_26_out);
  Multiplexer #(.width(32)) multiplexer_8 (.in0(multiplexer_7_out), .in1({32{1'b0}}), .out(alu_result_new), .sel(in_1));
  Register #(.width(32)) register_5 (.D(out_9), .en(or_4_out), .clk(in_2), .Q(out_10_t), .clr(in_1));
  Multiplexer multiplexer_9 (.in0(or_6_out), .in1(1'b0), .out(out_6), .sel(in_1));
  Multiplexer #(.width(32)) multiplexer_10 (.in0(multiplexer_18_out), .in1({32{1'b0}}), .out(out_7), .sel(in_1));
  Multiplexer multiplexer_11 (.in0(is_lw), .in1(1'b0), .out(out_8), .sel(in_1));
  Multiplexer multiplexer_12 (.in0(wpc), .in1(1'b0), .out(out_10), .sel(in_1));
  Multiplexer #(.width(32)) multiplexer_13 (.in0(multiplexer_17_out), .in1({32{1'b0}}), .out(out_11), .sel(in_1));
  Multiplexer multiplexer_14 (.in0(or_8_out), .in1(1'b0), .out(out_12), .sel(in_1));
  Multiplexer #(.width(5)) multiplexer_15 (.in0(multiplexer_19_out), .in1({5{1'b0}}), .out(out_13), .sel(in_1));
  and and_19 (and_19_out, is_old, demultiplexer_1_out11);
  or or_5 (or_5_out, and_19_out, and_28_out);
  Register #(.width(32)) register_6 (.D(out_9), .en(or_5_out), .clk(in_2), .Q(out_11_t), .clr(in_1));
  or or_6 (or_6_out, is_swsp, is_sw);
  Multiplexer #(.width(32)) multiplexer_16 (.in0({32{1'b0}}), .in1(multiplexer_20_out), .out(out_14), .sel(out_12));
  and and_20 (and_20_out, is_old, demultiplexer_1_out12);
  or or_7 (or_7_out, and_20_out, and_29_out);
  Multiplexer #(.width(32)) multiplexer_17 (.in0({32{1'b0}}), .in1(dpc), .out(multiplexer_17_out), .sel(\do ));
  assign swsp_imm = {{24{1'b0}}, {in_3[8:7], in_3[12:9], 2'b00}};  // Bit_Extender bit_extender_2
  Register #(.width(32)) register_7 (.D(out_9), .en(or_7_out), .clk(in_2), .Q(out_12_t), .clr(in_1));
  Multiplexer #(.width(32)) multiplexer_18 (
    .in0(multiplexer_23_out), .in1(alu_mv), .out(multiplexer_18_out), .sel(is_swsp));
  or or_8 (or_8_out, is_new, is_old);
  Multiplexer #(.width(5)) multiplexer_19 (
    .in0(multiplexer_26_out), .in1(reg_wsel), .out(multiplexer_19_out), .sel(is_old));
  Multiplexer #(.width(32)) multiplexer_20 (
    .in0(alu_new), .in1(alu_result_old), .out(multiplexer_20_out), .sel(is_old));
  or or_9 (is_old, is_add, is_mv, is_addi, is_slli, is_li, is_lui);
  or or_10 (is_new, is_addi4spn, is_lw);
  and and_21 (and_21_out, is_old, demultiplexer_1_out13);
  or or_11 (or_11_out, and_21_out, and_30_out);
  Register #(.width(32)) register_8 (.D(out_9), .en(or_11_out), .clk(in_2), .Q(out_13_t), .clr(in_1));
  Adder #(.width(32)) adder_7 (.a(offset_j), .b(in_5), .out(alu_j));  // open: cin, cout
  Adder #(.width(32)) adder_8 (.a(offset_beqz), .b(in_5), .out(alu_beqz));  // open: cin, cout
  Multiplexer #(.width(32)) multiplexer_21 (.in0({32{1'b0}}), .in1(alu_lui), .out(multiplexer_21_out), .sel(is_lui));
  and and_22 (and_22_out, is_old, demultiplexer_1_out14);
  or or_12 (or_12_out, and_22_out, and_31_out);
  Multiplexer #(.select(3), .width(32)) multiplexer_22 (
    .in0(out_8_t), .in1(out_9_t), .in2(out_10_t), .in3(out_11_t), .in4(out_12_t), .in5(out_13_t),
    .in6(out_14_t), .in7(out_15), .out(alu_sw), .sel(in_3[4:2]));
  Multiplexer #(.width(32)) multiplexer_23 (.in0({32{1'b0}}), .in1(alu_sw), .out(multiplexer_23_out), .sel(is_sw));
  assign addi4spn_imm = {{22{1'b0}}, {in_3[10:7], in_3[12:11], in_3[5], in_3[6], 2'b00}};  // Bit_Extender bit_extender_3
  Multiplexer #(.width(32)) multiplexer_24 (
    .in0(alu_result_new), .in1(alu_result_old), .out(multiplexer_24_out), .sel(is_old));
  Register #(.width(32)) register_9 (.D(out_9), .en(or_12_out), .clk(in_2), .Q(out_14_t), .clr(in_1));
  Multiplexer #(.width(32)) multiplexer_25 (
    .in0(multiplexer_21_out), .in1(alu_li), .out(multiplexer_25_out), .sel(is_li));
  and and_23 (and_23_out, is_old, demultiplexer_1_out15);
  or or_13 (or_13_out, and_23_out, and_32_out);
  Register #(.width(32)) register_10 (.D(out_9), .en(or_13_out), .clk(in_2), .Q(out_15), .clr(in_1));
  Multiplexer #(.width(5)) multiplexer_26 (.in0({5{1'b0}}), .in1(new_reg_sel), .out(multiplexer_26_out), .sel(is_new));
  Multiplexer #(.width(32)) multiplexer_27 (
    .in0(multiplexer_24_out), .in1(alu_j), .out(multiplexer_27_out), .sel(is_j));
  Multiplexer #(.select(3), .width(32)) multiplexer_28 (
    .in0(out_8_t), .in1(out_9_t), .in2(out_10_t), .in3(out_11_t), .in4(out_12_t), .in5(out_13_t),
    .in6(out_14_t), .in7(out_15), .out(rs1_new), .sel(in_3[9:7]));
  Multiplexer #(.width(32)) multiplexer_29 (
    .in0(multiplexer_25_out), .in1(alu_slli), .out(multiplexer_29_out), .sel(is_slli));
  Multiplexer #(.width(32)) multiplexer_30 (
    .in0(multiplexer_36_out), .in1(alu_addi4spn), .out(alu_new), .sel(is_addi4spn));
  Multiplexer #(.width(32)) multiplexer_31 (
    .in0(multiplexer_27_out), .in1(alu_jr), .out(multiplexer_31_out), .sel(is_jr));
  Multiplexer #(.width(32)) multiplexer_32 (
    .in0(multiplexer_29_out), .in1(alu_addi), .out(multiplexer_32_out), .sel(is_addi));
  Multiplexer #(.width(32)) multiplexer_33 (
    .in0(multiplexer_32_out), .in1(alu_mv), .out(multiplexer_33_out), .sel(is_mv));
  Multiplexer #(.width(32)) multiplexer_34 (.in0(multiplexer_31_out), .in1(alu_beqz), .out(out_9), .sel(is_beqz));
  assign bit_extender_4_out = {{2{1'b0}}, in_3[4:2]};  // Bit_Extender bit_extender_4
  Multiplexer #(.width(32)) multiplexer_35 (.in0({32{1'b0}}), .in1(offset_j), .out(multiplexer_35_out), .sel(is_j));
  Demultiplexer #(.select(3)) demultiplexer_2 (
    .out0(demultiplexer_2_out0), .out1(demultiplexer_2_out1), .out2(demultiplexer_2_out2),
    .out3(demultiplexer_2_out3), .out4(demultiplexer_2_out4), .out5(demultiplexer_2_out5),
    .out6(demultiplexer_2_out6), .out7(demultiplexer_2_out7), .in(1'b1), .sel(in_3[4:2]));
  Multiplexer #(.width(32)) multiplexer_36 (.in0({32{1'b0}}), .in1(in_4), .out(multiplexer_36_out), .sel(is_lw));
  Multiplexer #(.width(32)) multiplexer_37 (
    .in0(multiplexer_33_out), .in1(alu_add), .out(multiplexer_37_out), .sel(is_add));
  and and_24 (and_24_out, is_new, demultiplexer_2_out0);
  Adder #(.width(5)) adder_9 (.a(bit_extender_4_out), .b(5'b01000), .out(new_reg_sel));  // open: cin, cout
  assign uimm_lsw = {{25{1'b0}}, {in_3[5], in_3[12:10], in_3[6], 2'b00}};  // Bit_Extender bit_extender_5
  Comparator #(.width(32)) comparator_31 (.a(rs1_new), .b({32{1'b0}}), .eq(comparator_31_eq));  // open: gt, lt
  Multiplexer #(.width(32)) multiplexer_38 (
    .in0(multiplexer_37_out), .in1({32{1'b0}}), .out(alu_result_old), .sel(in_1));
  and and_25 (and_25_out, is_new, demultiplexer_2_out1);
  or or_14 (\do , is_j, is_beqz, is_jr);
  and and_26 (and_26_out, is_new, demultiplexer_2_out2);
  and and_27 (and_27_out, comparator_31_eq, is_beqz);
  and and_28 (and_28_out, is_new, demultiplexer_2_out3);
  Multiplexer #(.width(32)) multiplexer_39 (
    .in0(multiplexer_35_out), .in1(offset_beqz), .out(multiplexer_39_out), .sel(is_beqz));
  or or_15 (wpc, and_27_out, is_j, is_jr);
  and and_29 (and_29_out, is_new, demultiplexer_2_out4);
  and and_30 (and_30_out, is_new, demultiplexer_2_out5);
  Adder #(.width(32)) adder_10 (.a(multiplexer_39_out), .b(in_5), .out(adder_10_out));  // open: cin, cout
  and and_31 (and_31_out, is_new, demultiplexer_2_out6);
  and and_32 (and_32_out, is_new, demultiplexer_2_out7);
  Multiplexer #(.width(32)) multiplexer_40 (.in0(adder_10_out), .in1(alu_jr), .out(dpc), .sel(is_jr));
  assign offset_beqz = {{23{in_3[12]}}, {in_3[12], in_3[6:5], in_3[2], in_3[11:10], in_3[4:3], 1'b0}};  // Bit_Extender bit_extender_6
  assign offset_j = {{20{in_3[12]}}, {in_3[12], in_3[8], in_3[10:9], in_3[6], in_3[7], in_3[2], in_3[11], in_3[5:3], 1'b0}};  // Bit_Extender bit_extender_7

  // Other names for the same wires on the sheet: i2_4[2:0] = in_3[4:2]; i2_6[4:0] = in_3[6:2];
  //   i2_12[10:0] = in_3[12:2]; inst[15:0] = in_3; reg_wsel_new[2:0] = in_3[4:2]; sel_rd_new[2:0] = in_3[4:2];
  //   sel_rs2[4:0] = in_3[6:2]; uimm[4:0] = in_3[6:2]; i5_6[1:0] = in_3[6:5]; i5_12[7:0] = in_3[12:5];
  //   i7_11[4:0] = in_3[11:7]; i10_12[2:0] = in_3[12:10]; i7_9[2:0] = in_3[9:7]; sel_rs1_new[2:0] = in_3[9:7];
  //   i12 = in_3[12]; i12_15[3:0] = in_3[15:12]; clk = in_2; control_en = out_10; control_pc[31:0] = out_11;
  //   current_pc[31:0] = in_5; i0_1[1:0] = in_3[1:0]; i13_15[2:0] = in_3[15:13]; mem_din[31:0] = out_7;
  //   mem_ren = out_8; alu_lw[31:0] = in_4; mem_result[31:0] = in_4; mem_wen = out_6; rd[31:0] = alu_jr;
  //   rd_new[31:0] = alu_sw; alu_result[31:0] = out_9; reg_wd[31:0] = out_9; alu_swsp[31:0] = alu_mv;
  //   rs2[31:0] = alu_mv; rst = in_1; sel_rd[4:0] = reg_wsel; simm[31:0] = alu_li; wb_addr[4:0] = out_13;
  //   wb_data[31:0] = out_14; wb_en = out_12

  // Notes on the sheet:
  //   Fixed I/O
  //   Don't touch
endmodule

module testbench (
  input  rst,
  output mem_wen,
  output [31:0] mem_din,
  output mem_ren,
  output [31:0] mem_addr,
  output control_en,
  output [31:0] control_pc,
  output halt,
  output wb_en,
  output [4:0] wb_addr,
  output [31:0] wb_data
);

  wire clk, inst_en, not_1_out, not_2_out, not_3_out, not_4_out, por_1_out, rst_t;
  wire [15:0] inst, inst_i;
  wire [31:0] current_pc, inst_addr, mem_result;

  not not_1 (not_1_out, inst_i[0]);
  not not_2 (not_2_out, inst_i[1]);
  not not_3 (not_3_out, inst_i[13]);
  not not_4 (not_4_out, inst_i[14]);
  and and_1 (halt, not_1_out, not_2_out, not_3_out, not_4_out, inst_i[15]);
  Clock clock_1 (.out(clk));
  or or_1 (rst_t, rst, por_1_out);
  POR por_1 (.out(por_1_out));
  inst_fetch inst_fetch_1 (
    .clk(clk), .rst(rst_t), .control_en_i(control_en), .control_pc_i(control_pc), .inst_i(inst_i),
    .inst_en_o(inst_en), .current_pc_o(current_pc), .inst_addr_o(inst_addr), .inst_o(inst));
  TOP top_1 (
    .in_1(rst_t), .in_2(clk), .in_3(inst), .in_4(mem_result), .in_5(current_pc), .out_6(mem_wen),
    .out_7(mem_din), .out_8(mem_ren), .out_9(mem_addr), .out_10(control_en), .out_11(control_pc),
    .out_12(wb_en), .out_13(wb_addr), .out_14(wb_data));
  ROM #(.dataWidth(16)) rom_1 (.addr(inst_addr[7:0]), .data(inst_i));
  RAM #(.addrWidth(16), .asyncread("true"), .clearpin("true"), .dataWidth(32), .\type ("nonvolatile")) ram_1 (
    .addr(mem_addr[15:0]), .we(mem_wen), .oe(mem_ren), .clk(clk), .din(mem_din), .dout(mem_result),
    .clr(rst_t));

  // Notes on the sheet:
  //   contents of rom_1 (hex, n*v repeats v):
  //   4409 147d c011 bffd 1 1 4111 5429 c422 44b5 48 8482 8526 414c 511 c148 8000
  //   you can write any instruction in
endmodule
